# Fritzing sketch clock_module_smd_v1.2 (saved by Fritzing 0.9.3b)
circuit board: 6.9cm x 6.9cm
breadboards: 2

parts:
  G_+5_S_D_C = female pin header, 5 pins [form="♀ (female)"]
  NANO = Arduino Nano (Rev3.0)
  ID = double row male pin header, 8 pins [form="♂ (male)"]
  D3 = smd LED [color="Red (633nm)" package="0805 [SMD]"]
  R1 = Resistor [tolerance=±5% resistance=330 package="0805 [SMD]"]
  R4 = Resistor [tolerance=±5% resistance=330 package="0805 [SMD]"]
  D9 = smd LED [color="Red (633nm)" package="0805 [SMD]"]
  R3 = Resistor [tolerance=±5% resistance=330 package="0805 [SMD]"]
  D6 = smd LED [color="Red (633nm)" package="0805 [SMD]"]
  R2 = Resistor [tolerance=±5% resistance=330 package="0805 [SMD]"]
  D12 = smd LED [color="Red (633nm)" package="0805 [SMD]"]
  bit8 = Resistor [tolerance=±5% resistance=10k package="0805 [SMD]"]
  bit4 = Resistor [tolerance=±5% resistance=10k package="0805 [SMD]"]
  bit2 = Resistor [tolerance=±5% resistance=10k package="0805 [SMD]"]
  bit0 = Resistor [tolerance=±5% resistance=10k package="0805 [SMD]"]
  D1 = smd LED [color="Red (633nm)" package="0805 [SMD]"]
  D2 = smd LED [color="Red (633nm)" package="0805 [SMD]"]
  D8 = smd LED [color="Red (633nm)" package="0805 [SMD]"]
  D7 = smd LED [color="Red (633nm)" package="0805 [SMD]"]
  D5 = smd LED [color="Red (633nm)" package="0805 [SMD]"]
  D4 = smd LED [color="Red (633nm)" package="0805 [SMD]"]
  D10 = smd LED [color="Red (633nm)" package="0805 [SMD]"]
  D11 = smd LED [color="Red (633nm)" package="0805 [SMD]"]
  C1 = Ceramic Capacitor [capacitance=4.7µF package="0805 [SMD, multilayer]"]
  C2 = Ceramic Capacitor [capacitance=100nF package="0805 [SMD, multilayer]"]
  VID28-05 = Motor- VID28 [part_number=VID28-05 package=motor-64mm]

nets:
  GND: G_+5_S_D_C.pin1, NANO.GND, ID.pin1, ID.pin2, ID.pin3, ID.pin4, C1.0, C2.0
  5V: G_+5_S_D_C.pin2, NANO.VIN, bit8.Pin_0, bit4.Pin_0, bit2.Pin_0, bit0.Pin_0, C1.1, C2.1
  SYNC: G_+5_S_D_C.pin3, NANO.D2
  SDA: G_+5_S_D_C.pin4, NANO.D4
  SCL: G_+5_S_D_C.pin5, NANO.D5
  Col1: NANO.D1/TX, D3.cathode, D1.cathode, D2.cathode, D4.cathode
  Col3: NANO.D0/RX, D9.cathode, D12.cathode, D10.cathode, D11.cathode
  Col2: NANO.D3, D6.cathode, D8.cathode, D7.cathode, D5.cathode
  D6: NANO.D6, VID28-05.pin_A4
  D7: NANO.D7, VID28-05.pin_A3
  D8: NANO.D8, VID28-05.pin_A1
  D9: NANO.D9, VID28-05.pin_A2
  D10: NANO.D10, VID28-05.pin_B2
  D11: NANO.D11/MOSI, VID28-05.pin_B1
  D12: NANO.D12/MISO, VID28-05.pin_B3
  Row4: NANO.A7, R4.Pin_1
  Row3: NANO.A6, R3.Pin_1
  Row2: NANO.A5, R2.Pin_1
  Row1: NANO.A4, R1.Pin_1
  N1: NANO.A3, ID.pin5, bit8.Pin_1
  N2: NANO.A2, ID.pin6, bit4.Pin_1
  N3: NANO.A1, ID.pin7, bit2.Pin_1
  N4: NANO.A0, ID.pin8, bit0.Pin_1
  D13: NANO.D13/SCK, VID28-05.pin_B4
  N5: D3.anode, R3.Pin_0, D7.anode, D11.anode
  N6: R1.Pin_0, D9.anode, D1.anode, D5.anode
  N7: R4.Pin_0, D12.anode, D8.anode, D4.anode
  N8: D6.anode, R2.Pin_0, D2.anode, D10.anode

notes:
  SIG-in / (signal in)
  1 - GND
  2 - +5
  3 - Sync/D2
  4 - SDA/D4
  5 - SCL/D5
  SW1
  1 - ID-bit 3 / A3
  2 - ID-bit 2 / A2
  3 - ID-bit 1 / A1
  4 - ID-bit 0 / A0
  A2
  1
  2
  4
  8
  col1
  col3
  col2
  ClockWall project, 1.2
  ea. 10k pullups
  CodeValue Clock-Module
  v1.2, 2017-09-19
  CodeValue Clock-Module, v1.2

custom parts:
  Motor- VID28: VID28-05 motor
