# Fritzing sketch clock_module_v1.2 (saved by Fritzing 0.9.3b)
circuit board: 9cm x 8.3cm
breadboards: 2

parts:
  PIXELS = female pin header, 3 pins [form="♀ (female)"]
  A1 = female pin header, 2 pins [form="♀ (female)"]
  SENSOR = female pin header, 4 pins [form="♀ (female)"]
  R1 = Resistor [tolerance=±5% resistance=470 package=THT]
  NANO = Arduino Nano (Rev3.0) (ICSP)
  B2 = female pin header, 2 pins [form="♀ (female)"]
  B3 = female pin header, 2 pins [form="♀ (female)"]
  A4 = female pin header, 2 pins [form="♀ (female)"]
  SIG-out = female pin header, 6 pins [form="♀ (female)"]
  SIG-in = female pin header, 6 pins [form="♀ (female)"]
  SW1 = DIP SWITCH [package=dipswitch-02]
  SW2 = DIP SWITCH [package=dipswitch-02]
  VID28-05 = Motor- VID28 [part_number=VID28-05 package=motor-64mm]
  Part1 = 12 NeoPixel Ring [part_number=1643]
  C2 = Electrolytic Capacitor [capacitance=0.47mF voltage=16V package="100 mil [THT, electrolytic]"]
  C1 = Electrolytic Capacitor [capacitance=0.47mF voltage=16V package="100 mil [THT, electrolytic]"]

nets:
  N1: PIXELS.pin1, R1.Pin_1, Part1.IN
  5V: PIXELS.pin2, SENSOR.pin3, NANO.VIN, NANO.5V, SIG-out.pin3, SIG-in.pin3, Part1.VDD, C2.+, C1.+
  GND: PIXELS.pin3, SENSOR.pin4, NANO.GND, SIG-out.pin4, SIG-in.pin4, SW1.1, SW1.2, SW2.1, SW2.2, Part1.GND, C2.-, C1.-
  N2: A1.pin1, NANO.D5, VID28-05.pin_A2
  N3: A1.pin2, NANO.D4, VID28-05.pin_A1
  N4: SENSOR.pin1, NANO.A6
  N5: SENSOR.pin2, NANO.A7
  N6: R1.Pin_0, NANO.D6
  N7: NANO.D2, SIG-out.pin5, SIG-in.pin5
  N8: NANO.D3, SIG-out.pin6, SIG-in.pin6
  N9: NANO.D7, A4.pin2, VID28-05.pin_A3
  N10: NANO.D8, A4.pin1, VID28-05.pin_A4
  N11: NANO.D9, B2.pin2, VID28-05.pin_B1
  N12: NANO.D10, B2.pin1, VID28-05.pin_B2
  N13: NANO.D11/MOSI, B3.pin2, VID28-05.pin_B3
  N14: NANO.D12/MISO, B3.pin1, VID28-05.pin_B4
  N15: NANO.A5, SIG-out.pin1, SIG-in.pin1
  N16: NANO.A4, SIG-out.pin2, SIG-in.pin2
  N17: NANO.A3, SW1.4
  N18: NANO.A2, SW1.3
  N19: NANO.A1, SW2.4
  N20: NANO.A0, SW2.3

notes:
  SIG-in / (signal in)
  1 - SCL
  2 - SDA
  3 - VCC
  4 - GND
  5 - Sync / D2
  6 - CS / D3
  PIXELS
  1 - DIN / D6
  2 - 5v
  3 - GND
  SIG-OUT / (signal out)
  1 - SCL
  2 - SDA
  3- VCC
  4 - GND
  5 - Sync / D2
  6 - CS / D3
  SW1
  1 - ID-bit 3 / A3
  2 - ID-bit 2 / A2
  3 - ID-bit 1 / A1
  4 - ID-bit 0 / A0
  1
  +
  SENSORS
  1 - A6
  2 - A7
  3 - 5V
  4 - GND
  CodeValue clock-module v1.2
  B4
  A2
  A3
  B1
  in
  GND
  +5V
  VCC
  Sync
  D3
  SDA
  SCL

custom parts:
  Motor- VID28: VID28-05 motor
  12 NeoPixel Ring: 12 ultra bright smart LED NeoPixels are arranged in a circle with 1.5" (37mm) outer diameter. The rings are 'chainable' - connect the output pin of one to the input pin of another. Use only one microcontroller pin to control as many as you can chain together! Each LED is addressable as the driver chip is inside the LED. Each one has ~18mA constant current drive so the color will be very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
