# Fritzing sketch cluster controller (saved by Fritzing 0.9.3b)
circuit board: 5cm x 20cm
breadboards: 3

parts:
  U1 = Voltage Regulator - 5V [part_number=LM7805 package="TO220 [THT]"]
  U2 = Voltage Regulator - 5V [part_number=LM7805 package="TO220 [THT]"]
  WeMos_D1_Mini = WeMos D1 Mini
  U3 = Voltage Regulator - 5V [part_number=LM7805 package="TO220 [THT]"]
  U4 = Voltage Regulator - 5V [part_number=LM7805 package="TO220 [THT]"]
  J-3 = Header 2 [package=screwterminal-3.5mm-2_lock]
  SW1 = DIP Switch 4 Position [package=dipswitch-04]
  SEL_VCC = male pin header, 3 pins [form="♂ (male)"]
  J-2 = male pin header, 5 pins [form="♂ (male)"]
  J-1 = male pin header, 5 pins [form="♂ (male)"]
  LED2 = LED - 5mm [color="Green (555nm)" package="5 mm [THT]"]
  LED1 = LED - 5mm [color="Green (555nm)" package="5 mm [THT]"]
  LED4 = LED - 5mm [color="Green (555nm)" package="5 mm [THT]"]
  LED3 = LED - 5mm [color="Green (555nm)" package="5 mm [THT]"]
  C8 = Ceramic Capacitor [capacitance=100nF package="1206 [SMD, multilayer]"]
  C4 = Ceramic Capacitor [capacitance=100nF package="1206 [SMD, multilayer]"]
  C2 = Ceramic Capacitor [capacitance=100nF package="1206 [SMD, multilayer]"]
  C6 = Ceramic Capacitor [capacitance=100nF package="1206 [SMD, multilayer]"]
  R5 = Resistor [tolerance=±1% resistance=10k package="1206 [SMD]"]
  R4 = Resistor [tolerance=±1% resistance=80k package="1206 [SMD]"]
  R3 = Resistor [tolerance=±1% resistance=40k package="1206 [SMD]"]
  R2 = Resistor [tolerance=±1% resistance=20k package="1206 [SMD]"]
  R1 = Resistor [tolerance=±1% resistance=10k package="1206 [SMD]"]
  R9 = Resistor [tolerance=±5% resistance=1k package="1206 [SMD]"]
  R10 = Resistor [tolerance=±5% resistance=1k package="1206 [SMD]"]
  R11 = Resistor [tolerance=±5% resistance=1k package="1206 [SMD]"]
  R12 = Resistor [tolerance=±5% resistance=1k package="1206 [SMD]"]
  C1 = Electrolytic Capacitor [capacitance=1µF voltage=35V package="100 mil [THT, electrolytic]"]
  C3 = Electrolytic Capacitor [capacitance=1µF voltage=35V package="100 mil [THT, electrolytic]"]
  C5 = Electrolytic Capacitor [capacitance=1µF voltage=35V package="100 mil [THT, electrolytic]"]
  C7 = Electrolytic Capacitor [capacitance=1µF voltage=35V package="100 mil [THT, electrolytic]"]
  R13 = Resistor [tolerance=±1% resistance=4.7k package="1206 [SMD]"]
  R14 = Resistor [tolerance=±1% resistance=4.7k package="1206 [SMD]"]
  R15 = Resistor [tolerance=±1% resistance=10k package="1206 [SMD]"]
  J-D = male pin header, 5 pins [form="♂ (male)"]
  J-C = male pin header, 5 pins [form="♂ (male)"]
  J-B = male pin header, 5 pins [form="♂ (male)"]
  J-A = male pin header, 5 pins [form="♂ (male)"]

nets:
  12V: U1.input_voltage, U2.input_voltage, U3.input_voltage, U4.input_voltage, J-3.1, C1.+, C3.+, C5.+, C7.+
  GND: U1.GND, U2.GND, WeMos_D1_Mini.G, U3.GND, U4.GND, J-3.2, J-2.pin1, J-1.pin1, LED2.cathode, LED1.cathode, LED4.cathode, LED3.cathode, C8.0, C4.0, C2.0, C6.0, R5.Pin_1, C1.-, C3.-, C5.-, C7.-, J-D.pin5, J-C.pin5, J-B.pin5, J-A.pin5
  VCC_A: U1.output_voltage, SEL_VCC.pin3, C2.1, R9.Pin_1, J-A.pin4
  N1: U2.output_voltage, C4.1, R10.Pin_1, J-B.pin4
  3.3V: WeMos_D1_Mini.3V3, SW1.1, SW1.2, SW1.3, SW1.4
  5V: WeMos_D1_Mini.5V, SEL_VCC.pin2, R13.Pin_1, R14.Pin_1, R15.Pin_1
  buttons: WeMos_D1_Mini.A0, R5.Pin_0, R4.Pin_0, R3.Pin_0, R2.Pin_0, R1.Pin_0
  MASTER_SCL: WeMos_D1_Mini.D1, J-2.pin5, J-1.pin5
  MASTER_SDA: WeMos_D1_Mini.D2, J-2.pin4, J-1.pin4
  MASTER_SYNC: WeMos_D1_Mini.D3, J-2.pin3, J-1.pin3
  CLUSTER_SCL: WeMos_D1_Mini.D5, R13.Pin_0, J-D.pin1, J-C.pin1, J-B.pin1, J-A.pin1
  CLUSTER_SDA: WeMos_D1_Mini.D6, R14.Pin_0, J-D.pin2, J-C.pin2, J-B.pin2, J-A.pin2
  CLUSTER_SYNC: WeMos_D1_Mini.D7, R15.Pin_0, J-D.pin3, J-C.pin3, J-B.pin3, J-A.pin3
  N2: U3.output_voltage, C6.1, R11.Pin_1, J-C.pin4
  N3: U4.output_voltage, C8.1, R12.Pin_1, J-D.pin4
  N4: SW1.5, R4.Pin_1
  N5: SW1.6, R3.Pin_1
  N6: SW1.7, R2.Pin_1
  N7: SW1.8, R1.Pin_1
  Vin: SEL_VCC.pin1, J-2.pin2, J-1.pin2
  N8: LED2.anode, R10.Pin_0
  N9: LED1.anode, R9.Pin_0
  N10: LED4.anode, R12.Pin_0
  N11: LED3.anode, R11.Pin_0

notes:
  B1
  B2
  B4
  B8
  ID SWITCH
  CodeValue ClockWall
  Cluster Controller
  v1.0, 2017-10-09
  VIN
  Vcc_A
  +12v
  VCC
  GND
  3.3v
  +5v
  Jack-A ... to Clock Module Boards 0, 1, 2, 3
  Jack-B ... to Clock Module Boards 4, 5, 6, 7
  Jack-C ... to Clock Module Boards 8, 9, 10, 11
  Jack-D ... to Clock Module Boards 12, 13, 14, 15
  8  4  2  1
