# Fritzing sketch clock_module_v1.4d no LEDs (saved by Fritzing 0.9.3b)
circuit board: 10cm x 10cm
breadboards: 2

parts:
  NANO = Arduino Nano (Rev3.0) [part_number="A000005 (socketed)"]
  MOTOR = Motor- VID28 [part_number="VID28-05 or BKA30D-R5" package=motor-64mm]
  LDR1 = Photocell (LDR) [part_number=GL5528 package=THT]
  LDR2 = Photocell (LDR) [part_number=GL5528 package=THT]
  R14 = Resistor [tolerance=±1% resistance=10k package="1206 [SMD]"]
  R13 = Resistor [tolerance=±1% resistance=10k package="1206 [SMD]"]
  C1 = Electrolytic Capacitor [capacitance=47µF part_number=25MH547MEFC6.3X5 voltage=20V package="100 mil [THT, electrolytic]"]
  R18 = Resistor [tolerance=±1% resistance=80k package="1206 [SMD]"]
  R17 = Resistor [tolerance=±1% resistance=40k package="1206 [SMD]"]
  R16 = Resistor [tolerance=±1% resistance=20k package="1206 [SMD]"]
  R15 = Resistor [tolerance=±1% resistance=10k package="1206 [SMD]"]
  R19 = Resistor [tolerance=±1% resistance=10k package="1206 [SMD]"]
  SW1 = DIP Switch 4 Position [part_number="C&K BD04 or equiv." package=dipswitch-04]
  J2 = molex pin header, 5 pins [form=molex part_number="Female header"]
  J1 = molex pin header, 5 pins [form=molex part_number="Male Header"]
  C2 = Ceramic Capacitor [capacitance=100nF package="0805 [SMD, multilayer]"]

nets:
  GND: NANO.GND, R14.Pin_1, R13.Pin_1, C1.-, R19.Pin_1, J2.pin1, J1.pin1, C2.0
  SYNC: NANO.D2, J2.pin3, J1.pin3
  M_A1: NANO.D4, MOTOR.pin_A1
  M_A2: NANO.D5, MOTOR.pin_A2
  M_B3: NANO.D6, MOTOR.pin_B3
  M_B4: NANO.D7, MOTOR.pin_B4
  M-A3: NANO.D8, MOTOR.pin_A3
  M_A4: NANO.D9, MOTOR.pin_A4
  M-B2: NANO.D10, MOTOR.pin_B2
  M-B1: NANO.D12/MISO, MOTOR.pin_B1
  5V/REG. +5v: NANO.5V, LDR1.pin_1, LDR2.pin_1, C1.+, SW1.1, SW1.2, SW1.3, SW1.4, J2.pin2, J1.pin2, C2.1
  LDR2: NANO.A7, LDR2.pin_0, R14.Pin_0
  LDR1: NANO.A6, LDR1.pin_0, R13.Pin_0
  SCL: NANO.A5, J2.pin5, J1.pin5
  SDA: NANO.A4, J2.pin4, J1.pin4
  BUTTONS: NANO.A0, R18.Pin_1, R17.Pin_1, R16.Pin_1, R15.Pin_1, R19.Pin_0
  N1: R18.Pin_0, SW1.5
  N2: R17.Pin_0, SW1.6
  N3: R16.Pin_0, SW1.7
  N4: R15.Pin_0, SW1.8

notes:
  SIG-in / (signal in)
  1 - GND
  2 - +5
  3 - Sync/D2
  4 - SDA/D4
  5 - SCL/D5
  A2
  CodeValue Clock-Module
  v1.4, 2017-10-19
  CodeValue Clock-Module, v1.4
  Gnd
  +5V
  Sync
  Data
  CLK
  B1
  B2
  B4
  B8
  ID SWITCH
  8  4  2  1
  ID SWITCH
  1 - ID-bit 3 MSB
  2 - ID-bit 2
  3 - ID-bit 1
  4 - ID-bit 0 LSB
  CodeValue ClockWall Project, Clock Module, 1.4c

custom parts:
  Motor- VID28: VID28-05 motor
  Photocell (LDR): light dependent resistor (LDR), GL5516 or GL5528
