# Fritzing sketch clock_module_v1.4d (saved by Fritzing 0.9.3b)
circuit board: 10cm x 10cm
breadboards: 5

parts:
  NANO = Arduino Nano (Rev3.0) [part_number="A000005 (socketed)"]
  MOTOR = Motor- VID28 [part_number="VID28-05 or BKA30D-R5" package=motor-64mm]
  U2 = 74HC595 SMD [part_number="74HC595D, NXT SO16" package="SO16 [SMD]"]
  LDR1 = Photocell (LDR) [part_number=GL5528 package=THT]
  LDR2 = Photocell (LDR) [part_number=GL5528 package=THT]
  R2 = Resistor [tolerance=±1% resistance=330 package="1206 [SMD]"]
  R1 = Resistor [tolerance=±1% resistance=330 package="1206 [SMD]"]
  R3 = Resistor [tolerance=±1% resistance=330 package="1206 [SMD]"]
  R4 = Resistor [tolerance=±1% resistance=330 package="1206 [SMD]"]
  R5 = Resistor [tolerance=±1% resistance=330 package="1206 [SMD]"]
  R6 = Resistor [tolerance=±1% resistance=330 package="1206 [SMD]"]
  R14 = Resistor [tolerance=±1% resistance=10k package="1206 [SMD]"]
  R13 = Resistor [tolerance=±1% resistance=10k package="1206 [SMD]"]
  C1 = Electrolytic Capacitor [capacitance=47µF part_number=25MH547MEFC6.3X5 voltage=20V package="100 mil [THT, electrolytic]"]
  U1 = 74HC595 SMD [part_number="74HC595D, NXT SO16" package="SO16 [SMD]"]
  R18 = Resistor [tolerance=±1% resistance=80k package="1206 [SMD]"]
  R17 = Resistor [tolerance=±1% resistance=40k package="1206 [SMD]"]
  R16 = Resistor [tolerance=±1% resistance=20k package="1206 [SMD]"]
  R15 = Resistor [tolerance=±1% resistance=10k package="1206 [SMD]"]
  R19 = Resistor [tolerance=±1% resistance=10k package="1206 [SMD]"]
  SW1 = DIP Switch 4 Position [part_number="C&K BD04 or equiv." package=dipswitch-04]
  R8 = Resistor [tolerance=±1% resistance=330 package="1206 [SMD]"]
  R11 = Resistor [tolerance=±1% resistance=330 package="1206 [SMD]"]
  R10 = Resistor [tolerance=±1% resistance=330 package="1206 [SMD]"]
  R7 = Resistor [tolerance=±1% resistance=330 package="1206 [SMD]"]
  R12 = Resistor [tolerance=±1% resistance=330 package="1206 [SMD]"]
  R9 = Resistor [tolerance=±1% resistance=330 package="1206 [SMD]"]
  J2 = molex pin header, 5 pins [form=molex part_number="Female header"]
  J1 = molex pin header, 5 pins [form=molex part_number="Male Header"]
  C2 = Ceramic Capacitor [capacitance=100nF package="0805 [SMD, multilayer]"]
  C3 = Ceramic Capacitor [capacitance=100nF package="0805 [SMD, multilayer]"]
  C4 = Ceramic Capacitor [capacitance=100nF package="0805 [SMD, multilayer]"]
  D2 = LED - 3mm [color="Blue (470nm)" package="3 mm [THT]"]
  D1 = LED - 3mm [color="Blue (470nm)" package="3 mm [THT]"]
  D4 = LED - 3mm [color="Blue (470nm)" package="3 mm [THT]"]
  D5 = LED - 3mm [color="Blue (470nm)" package="3 mm [THT]"]
  D6 = LED - 3mm [color="Blue (470nm)" package="3 mm [THT]"]
  D3 = LED - 3mm [color="Blue (470nm)" package="3 mm [THT]"]
  D7 = LED - 3mm [color="Blue (470nm)" package="3 mm [THT]"]
  D8 = LED - 3mm [color="Blue (470nm)" package="3 mm [THT]"]
  D9 = LED - 3mm [color="Blue (470nm)" package="3 mm [THT]"]
  D10 = LED - 3mm [color="Blue (470nm)" package="3 mm [THT]"]
  D11 = LED - 3mm [color="Blue (470nm)" package="3 mm [THT]"]
  D12 = LED - 3mm [color="Blue (470nm)" package="3 mm [THT]"]

nets:
  GND: NANO.GND, U2.GND, R14.Pin_1, R13.Pin_1, C1.-, U1.GND, R19.Pin_1, J2.pin1, J1.pin1, C2.0, C3.1, C4.1, D2.cathode, D1.cathode, D4.cathode, D5.cathode, D6.cathode, D3.cathode, D7.cathode, D8.cathode, D9.cathode, D10.cathode, D11.cathode, D12.cathode
  SYNC: NANO.D2, J2.pin3, J1.pin3
  OE_: NANO.D3, U2.OE, U1.OE
  M_A1: NANO.D4, MOTOR.pin_A1
  M_A2: NANO.D5, MOTOR.pin_A2
  M_B3: NANO.D6, MOTOR.pin_B3
  M_B4: NANO.D7, MOTOR.pin_B4
  M-A3: NANO.D8, MOTOR.pin_A3
  M_A4: NANO.D9, MOTOR.pin_A4
  M-B2: NANO.D10, MOTOR.pin_B2
  MOSI: NANO.D11/MOSI, U1.DS
  M-B1: NANO.D12/MISO, MOTOR.pin_B1
  5V/REG. +5v: NANO.5V, U2.MR, U2.VCC, LDR1.pin_1, LDR2.pin_1, C1.+, U1.MR, U1.VCC, SW1.1, SW1.2, SW1.3, SW1.4, J2.pin2, J1.pin2, C2.1, C3.0, C4.0
  LDR2: NANO.A7, LDR2.pin_0, R14.Pin_0
  LDR1: NANO.A6, LDR1.pin_0, R13.Pin_0
  SCL: NANO.A5, J2.pin5, J1.pin5
  SDA: NANO.A4, J2.pin4, J1.pin4
  LATCH: NANO.A1, U2.ST_CP, U1.ST_CP
  BUTTONS: NANO.A0, R18.Pin_1, R17.Pin_1, R16.Pin_1, R15.Pin_1, R19.Pin_0
  SCLK: NANO.D13/SCK, U2.SH_CP, U1.SH_CP
  N1: U2.Q2, R7.Pin_0
  N2: U2.Q3, R8.Pin_0
  N3: U2.Q4, R9.Pin_0
  N4: U2.Q5, R10.Pin_0
  N5: U2.Q6, R11.Pin_0
  N6: U2.Q7, R12.Pin_0
  N7: U2.DS, U1.Q7'
  N8: R2.Pin_0, U1.Q3
  N9: R2.Pin_1, D2.anode
  N10: R1.Pin_0, U1.Q2
  N11: R1.Pin_1, D1.anode
  N12: R3.Pin_0, U1.Q4
  N13: R3.Pin_1, D3.anode
  N14: R4.Pin_0, U1.Q5
  N15: R4.Pin_1, D4.anode
  N16: R5.Pin_0, U1.Q6
  N17: R5.Pin_1, D5.anode
  N18: R6.Pin_0, U1.Q7
  N19: R6.Pin_1, D6.anode
  N20: R18.Pin_0, SW1.5
  N21: R17.Pin_0, SW1.6
  N22: R16.Pin_0, SW1.7
  N23: R15.Pin_0, SW1.8
  N24: R8.Pin_1, D8.anode
  N25: R11.Pin_1, D11.anode
  N26: R10.Pin_1, D10.anode
  N27: R7.Pin_1, D7.anode
  N28: R12.Pin_1, D12.anode
  N29: R9.Pin_1, D9.anode

notes:
  SIG-in / (signal in)
  1 - GND
  2 - +5
  3 - Sync/D2
  4 - SDA/D4
  5 - SCL/D5
  A2
  CodeValue Clock-Module
  v1.4, 2017-10-22
  CodeValue Clock-Module, v1.4
  Gnd
  +5V
  Sync
  Data
  CLK
  B1
  B2
  B4
  B8
  ID SWITCH
  8  4  2  1
  ID SWITCH
  1 - ID-bit 3 MSB
  2 - ID-bit 2
  3 - ID-bit 1
  4 - ID-bit 0 LSB
  MOSI
  OE
  LATCH
  SCLK
  CodeValue ClockWall Project, Clock Module, 1.4d
  LDRs - resistance as a function of expected light levels in both states - make sure the resulting voltage divider output in each state (depending on chosen resistor value) gives readily determined "state" of light sensor
  Revisit I2C pullup resistor values, maybe a fanout of 16 is too much, lower resistor value or add buffers
  Maybe use two OEs for hc595s so peak led currents can be out of phase
  R1 and R7 - assuming Vf 2.0v for the blue leds, and Voh of 595 at Ioh of LED current is 5.0V, 3V drop across resistor, 330 ohms gives 10 mA per LED (check assumptions)

custom parts:
  Motor- VID28: VID28-05 motor
  Photocell (LDR): light dependent resistor (LDR), GL5516 or GL5528
