# Fritzing sketch clock_module_smd_v1.3 (saved by Fritzing 0.9.3b)
circuit board: 10cm x 10cm
breadboards: 5

parts:
  NANO = Arduino Nano (Rev3.0) [part_number="Nano, socketed"]
  D3 = smd LED [color="Blue (505nm)" package="0805 [SMD]"]
  D9 = smd LED [color="Blue (505nm)" package="0805 [SMD]"]
  D6 = smd LED [color="Blue (505nm)" package="0805 [SMD]"]
  D12 = smd LED [color="Blue (505nm)" package="0805 [SMD]"]
  D1 = smd LED [color="Blue (505nm)" package="0805 [SMD]"]
  D2 = smd LED [color="Blue (505nm)" package="0805 [SMD]"]
  D8 = smd LED [color="Blue (505nm)" package="0805 [SMD]"]
  D7 = smd LED [color="Blue (505nm)" package="0805 [SMD]"]
  D5 = smd LED [color="Blue (505nm)" package="0805 [SMD]"]
  D4 = smd LED [color="Blue (505nm)" package="0805 [SMD]"]
  D10 = smd LED [color="Blue (505nm)" package="0805 [SMD]"]
  D11 = smd LED [color="Blue (505nm)" package="0805 [SMD]"]
  VID28-05 = Motor- VID28 [part_number="VID28-05 or equiv." package=motor-64mm]
  R16 = Resistor [tolerance=±1% resistance=2.2k package="0805 [SMD]"]
  R15 = Resistor [tolerance=±1% resistance=2.2k package="0805 [SMD]"]
  R14 = Resistor [tolerance=±1% resistance=2.2k package="0805 [SMD]"]
  R13 = Resistor [tolerance=±1% resistance=2.2k package="0805 [SMD]"]
  C1 = Ceramic Capacitor [capacitance=4.7µF package="0805 [SMD, multilayer]"]
  C2 = Ceramic Capacitor [capacitance=100nF package="0805 [SMD, multilayer]"]
  R12 = Resistor [tolerance=±5% resistance=330 package="0805 [SMD]"]
  R11 = Resistor [tolerance=±5% resistance=330 package="0805 [SMD]"]
  R10 = Resistor [tolerance=±5% resistance=330 package="0805 [SMD]"]
  R9 = Resistor [tolerance=±5% resistance=330 package="0805 [SMD]"]
  R7 = Resistor [tolerance=±5% resistance=330 package="0805 [SMD]"]
  R8 = Resistor [tolerance=±5% resistance=330 package="0805 [SMD]"]
  U2 = 74HC595 SMD [part_number="74HC595 D" package="SO16 [SMD]"]
  U1 = 74HC595 SMD [part_number="74HC595 D" package="SO16 [SMD]"]
  R6 = Resistor [tolerance=±5% resistance=330 package="0805 [SMD]"]
  R5 = Resistor [tolerance=±5% resistance=330 package="0805 [SMD]"]
  R4 = Resistor [tolerance=±5% resistance=330 package="0805 [SMD]"]
  R3 = Resistor [tolerance=±5% resistance=330 package="0805 [SMD]"]
  R2 = Resistor [tolerance=±5% resistance=330 package="0805 [SMD]"]
  R1 = Resistor [tolerance=±5% resistance=330 package="0805 [SMD]"]
  R18 = Resistor [tolerance=±5% resistance=10k package="0805 [SMD]"]
  R19 = Resistor [tolerance=±5% resistance=10k package="0805 [SMD]"]
  LDR1 = Photocell (LDR) [part_number=GL5528 package=THT]
  LDR2 = Photocell (LDR) [part_number=GL5528 package=THT]
  CONN2 = male pin header, 5 pins [form="♂ (male)"]
  CONN1 = male pin header, 5 pins [form="♂ (male)"]
  SW1 = DIP Switch 4 Position [package=dipswitch-04]
  R20 = Resistor [tolerance=±1% resistance=2.2k package="0805 [SMD]"]
  R21 = Resistor [tolerance=±1% resistance=1k package="0805 [SMD]"]
  R22 = Resistor [tolerance=±1% resistance=1k package="0805 [SMD]"]
  R23 = Resistor [tolerance=±1% resistance=1k package="0805 [SMD]"]

nets:
  GND: NANO.GND, D3.cathode, D9.cathode, D6.cathode, D12.cathode, D1.cathode, D2.cathode, D8.cathode, D7.cathode, D5.cathode, D4.cathode, D10.cathode, D11.cathode, C1.0, C2.0, U2.GND, U1.GND, R18.Pin_1, R19.Pin_1, CONN2.pin1, CONN1.pin1, R20.Pin_1
  SYNC: NANO.D2, CONN2.pin3, CONN1.pin3
  OE_: NANO.D3, U2.OE, U1.OE
  M_A1: NANO.D4, VID28-05.pin_A1
  M_A2: NANO.D5, VID28-05.pin_A2
  M_B3: NANO.D6, VID28-05.pin_B3
  M_B4: NANO.D7, VID28-05.pin_B4
  M-A3: NANO.D8, VID28-05.pin_A3
  M_A4: NANO.D9, VID28-05.pin_A4
  M-B2: NANO.D10, VID28-05.pin_B2
  MOSI: NANO.D11/MOSI, U1.DS
  M-B1: NANO.D12/MISO, VID28-05.pin_B1
  5V: NANO.VIN, C1.1, C2.1, U2.MR, U2.VCC, U1.MR, U1.VCC, LDR1.pin_1, LDR2.pin_1, CONN2.pin2, CONN1.pin2, SW1.1, SW1.2, SW1.3, SW1.4
  LDR2: NANO.A7, R19.Pin_0, LDR2.pin_0
  LDR1: NANO.A6, R18.Pin_0, LDR1.pin_0
  SCL: NANO.A5, CONN2.pin5, CONN1.pin5
  SDA: NANO.A4, CONN2.pin4, CONN1.pin4
  LATCH: NANO.A1, U2.ST_CP, U1.ST_CP
  buttons: NANO.A0, R13.Pin_0, R23.Pin_0
  SCLK: NANO.D13/SCK, U2.SH_CP, U1.SH_CP
  N1: D3.anode, R3.Pin_1
  N2: D9.anode, R9.Pin_1
  N3: D6.anode, R6.Pin_1
  N4: D12.anode, R12.Pin_1
  N5: D1.anode, R1.Pin_1
  N6: D2.anode, R2.Pin_1
  N7: D8.anode, R8.Pin_1
  N8: D7.anode, R7.Pin_1
  N9: D5.anode, R5.Pin_1
  N10: D4.anode, R4.Pin_1
  N11: D10.anode, R10.Pin_1
  N12: D11.anode, R11.Pin_1
  N13: R16.Pin_0, R20.Pin_0, R21.Pin_1
  N14: R16.Pin_1, SW1.5
  N15: R15.Pin_0, R21.Pin_0, R22.Pin_1
  N16: R15.Pin_1, SW1.6
  N17: R14.Pin_0, R22.Pin_0, R23.Pin_1
  N18: R14.Pin_1, SW1.7
  N19: R13.Pin_1, SW1.8
  N20: R12.Pin_0, U2.Q7
  N21: R11.Pin_0, U2.Q6
  N22: R10.Pin_0, U2.Q5
  N23: R9.Pin_0, U2.Q4
  N24: R7.Pin_0, U2.Q2
  N25: R8.Pin_0, U2.Q3
  N26: U2.DS, U1.Q7'
  N27: U1.Q2, R1.Pin_0
  N28: U1.Q3, R2.Pin_0
  N29: U1.Q4, R3.Pin_0
  N30: U1.Q5, R4.Pin_0
  N31: U1.Q6, R5.Pin_0
  N32: U1.Q7, R6.Pin_0

notes:
  SIG-in / (signal in)
  1 - GND
  2 - +5
  3 - Sync/D2
  4 - SDA/D4
  5 - SCL/D5
  ID SWITCH
  1 - ID-bit 3 MSB
  2 - ID-bit 2
  3 - ID-bit 1
  4 - ID-bit 0 LSB
  A2
  ClockWall project, 1.2
  CodeValue Clock-Module
  v1.3, 2017-09-29
  CodeValue Clock-Module, v1.3
  Gnd
  +5V
  Sync
  Data
  CLK
  CONN2
  CONN1
  D0
  D1
  D2
  D3
  ID SWITCH

custom parts:
  Motor- VID28: VID28-05 motor
  Photocell (LDR): light dependent resistor (LDR), GL5516 or GL5528
