# Fritzing sketch clock_module_v1.5 noLEDs (saved by Fritzing 0.9.3b)
circuit board: 10cm x 10cm
breadboards: 1

parts:
  NANO = Arduino Nano (Rev3.0) [part_number="A000005 (socketed)"]
  MOTOR = Motor- VID28 [part_number=BKA30D-R5 package=motor-64mm]
  LDR1 = Photocell (LDR) [part_number=GL5528 package=THT]
  LDR2 = Photocell (LDR) [part_number=GL5528 package=THT]
  SW1 = DIP Switch 4 Position [part_number="C&K BD04 or equiv." package=dipswitch-04]
  C1 = Electrolytic Capacitor [capacitance=47µF voltage=16V package="0605 [SMD, electrolytic]"]
  C3 = Ceramic Capacitor [capacitance=1µF package="0805 [SMD, multilayer]"]
  C2 = Ceramic Capacitor [capacitance=1µF package="0805 [SMD, multilayer]"]
  R2 = Resistor [tolerance=±1% resistance=10k package="0805 [SMD]"]
  R1 = Resistor [tolerance=±1% resistance=10k package="0805 [SMD]"]
  J2 = molex pin header, 5 pins [form=molex]
  J1 = molex pin header, 5 pins [form=molex]

nets:
  GND: NANO.GND, SW1.1, SW1.2, SW1.3, SW1.4, C1.-, C3.0, C2.0, R2.Pin_1, R1.Pin_1, J2.pin1, J1.pin1
  SYNC: NANO.D2, J2.pin3, J1.pin3
  M_A1: NANO.D4, MOTOR.pin_A1
  M_A2: NANO.D5, MOTOR.pin_A2
  M_B3: NANO.D6, MOTOR.pin_B3
  M_B4: NANO.D7, MOTOR.pin_B4
  M-A3: NANO.D8, MOTOR.pin_A3
  M_A4: NANO.D9, MOTOR.pin_A4
  M-B2: NANO.D10, MOTOR.pin_B2
  M-B1: NANO.D12/MISO, MOTOR.pin_B1
  5V/REG. +5v: NANO.5V, LDR1.pin_1, LDR2.pin_1, C1.+, C3.1, C2.1, J2.pin2, J1.pin2
  LDR2: NANO.A7, LDR2.pin_0, R2.Pin_0
  LDR1: NANO.A6, LDR1.pin_0, R1.Pin_0
  SCL: NANO.A5, J2.pin5, J1.pin5
  SDA: NANO.A4, J2.pin4, J1.pin4
  SW1-1: NANO.A3, SW1.8
  SW1-2: NANO.A2, SW1.7
  SW1-3: NANO.A1, SW1.6
  SW1-4: NANO.A0, SW1.5

notes:
  SIG-in / (signal in)
  1 - GND
  2 - +5
  3 - Sync/D2
  4 - SDA/D4
  5 - SCL/D5
  A2
  CodeValue Clock-Module
  v1.5, 2017-11-10
  CodeValue Clock-Module, v1.5
  Gnd
  +5V
  Sync
  Data
  CLK
  ID SWITCH
  8  4  2  1
  ID SWITCH
  1 - ID-bit 3 MSB
  2 - ID-bit 2
  3 - ID-bit 1
  4 - ID-bit 0 LSB
  CodeValue ClockWall Project, Clock Module, 1.4d
  LDRs - resistance as a function of expected light levels in both states - make sure the resulting voltage divider output in each state (depending on chosen resistor value) gives readily determined "state" of light sensor
  Revisit I2C pullup resistor values, maybe a fanout of 16 is too much, lower resistor value or add buffers

custom parts:
  Motor- VID28: VID28-05 motor
  Photocell (LDR): light dependent resistor (LDR), GL5516 or GL5528
