# Fritzing sketch Power Signal Dist 1.1 (saved by Fritzing 0.9.3b)
circuit board: 5cm x 20cm
breadboards: 1

parts:
  U1 = Voltage Regulator - 5V [part_number=LM7805 package="TO220 [THT]"]
  C2 = Ceramic Capacitor [capacitance=100nF package="1206 [SMD, multilayer]"]
  R1 = Resistor [tolerance=±1% resistance=1k package="1206 [SMD]"]
  C1 = Electrolytic Capacitor [capacitance=1µF voltage=35V package="100 mil [THT, electrolytic]"]
  J3/TP = male pin header, 3 pins [form="♂ (male)"]
  J-A = female pin header, 5 pins [form="♀ (female)"]
  J1 = female pin header, 5 pins [form="♀ (female)"]
  C3 = Electrolytic Capacitor [capacitance=1µF voltage=35V package="100 mil [THT, electrolytic]"]
  C4 = Ceramic Capacitor [capacitance=100nF package="1206 [SMD, multilayer]"]
  R2 = Resistor [tolerance=±1% resistance=1k package="1206 [SMD]"]
  U2 = Voltage Regulator - 5V [part_number=LM7805 package="TO220 [THT]"]
  J-B = female pin header, 5 pins [form="♀ (female)"]
  C5 = Electrolytic Capacitor [capacitance=1µF voltage=35V package="100 mil [THT, electrolytic]"]
  C6 = Ceramic Capacitor [capacitance=100nF package="1206 [SMD, multilayer]"]
  R3 = Resistor [tolerance=±1% resistance=1k package="1206 [SMD]"]
  U3 = Voltage Regulator - 5V [part_number=LM7805 package="TO220 [THT]"]
  J-C = female pin header, 5 pins [form="♀ (female)"]
  C7 = Electrolytic Capacitor [capacitance=1µF voltage=35V package="100 mil [THT, electrolytic]"]
  C8 = Ceramic Capacitor [capacitance=100nF package="1206 [SMD, multilayer]"]
  R4 = Resistor [tolerance=±1% resistance=1k package="1206 [SMD]"]
  U4 = Voltage Regulator - 5V [part_number=LM7805 package="TO220 [THT]"]
  J-D = female pin header, 5 pins [form="♀ (female)"]
  C9 = Ceramic Capacitor [capacitance=1µF voltage=6.3V package="1206 [SMD, multilayer]"]
  R5 = Resistor [tolerance=±1% resistance=220 package="1206 [SMD]"]
  J2/PWR = molex pin header, 3 pins [form=molex]
  LED1 = smd LED [color="Green (565nm)" package="1206 [SMD]"]
  LED2 = smd LED [color="Green (565nm)" package="1206 [SMD]"]
  LED5 = smd LED [color="Yellow (585nm)" package="1206 [SMD]"]
  LED3 = smd LED [color="Green (565nm)" package="1206 [SMD]"]
  LED4 = smd LED [color="Green (565nm)" package="1206 [SMD]"]

nets:
  12V: U1.input_voltage, C1.+, J3/TP.pin1, C3.+, U2.input_voltage, C5.+, U3.input_voltage, C7.+, U4.input_voltage, J2/PWR.pin2
  GND: U1.GND, C2.0, C1.-, J3/TP.pin3, J-A.pin1, J1.pin1, C3.-, C4.0, U2.GND, J-B.pin1, C5.-, C6.0, U3.GND, J-C.pin1, C7.-, C8.0, U4.GND, J-D.pin1, C9.0, J2/PWR.pin1, J2/PWR.pin3, LED1.cathode, LED2.cathode, LED5.cathode, LED3.cathode, LED4.cathode
  VCC_A: U1.output_voltage, C2.1, R1.Pin_1, J3/TP.pin2, J-A.pin2, J1.pin2, C9.1
  N1: R1.Pin_0, LED1.anode
  CLUSTER_SYNC: J-A.pin3, J1.pin3, J-B.pin3, J-C.pin3, J-D.pin3, R5.Pin_1
  CLUSTER_SDA: J-A.pin4, J1.pin4, J-B.pin4, J-C.pin4, J-D.pin4
  CLUSTER_SCL: J-A.pin5, J1.pin5, J-B.pin5, J-C.pin5, J-D.pin5
  N2: C4.1, R2.Pin_1, U2.output_voltage, J-B.pin2
  N3: R2.Pin_0, LED2.anode
  N4: C6.1, R3.Pin_1, U3.output_voltage, J-C.pin2
  N5: R3.Pin_0, LED3.anode
  N6: C8.1, R4.Pin_1, U4.output_voltage, J-D.pin2
  N7: R4.Pin_0, LED4.anode
  N8: R5.Pin_0, LED5.anode

notes:
  CodeValue ClockWall
  Power & Signal Distribution
  v1.1, 2018-01-14
  +12v
  GND
  +5
  Jack-A ... to Clock Module Boards 0, 1, 2, 3
  Jack-B ... to Clock Module Boards 4, 5, 6, 7
  Jack-C ... to Clock Module Boards 8, 9, 10, 11
  Jack-D ... to Clock Module Boards 12, 13, 14, 15
  ClockWall, CLockWall Power & Signal Distribution PCB, 1.0
  Jack-1 ... to Cluster Controller Board
  test point
  +12
  SYNC
  SDA
  SCL
  SYNC LED
  PWR-A
  PWR-B
  PWR-C
  PWR-D
