# Fritzing sketch Power Signal Dist 1.2 (saved by Fritzing 0.9.3b)
circuit board: 5cm x 20cm
breadboards: 1

parts:
  C2 = Ceramic Capacitor [capacitance=100nF package="1206 [SMD, multilayer]"]
  R1 = Resistor [tolerance=±1% resistance=220 package="1206 [SMD]"]
  C4 = Ceramic Capacitor [capacitance=100nF package="1206 [SMD, multilayer]"]
  R2 = Resistor [tolerance=±1% resistance=220 package="1206 [SMD]"]
  C6 = Ceramic Capacitor [capacitance=100nF package="1206 [SMD, multilayer]"]
  R3 = Resistor [tolerance=±1% resistance=220 package="1206 [SMD]"]
  C8 = Ceramic Capacitor [capacitance=100nF package="1206 [SMD, multilayer]"]
  R4 = Resistor [tolerance=±1% resistance=220 package="1206 [SMD]"]
  C9 = Ceramic Capacitor [capacitance=1µF voltage=6.3V package="1206 [SMD, multilayer]"]
  R5 = Resistor [tolerance=±1% resistance=220 package="1206 [SMD]"]
  J2/PWR = molex pin header, 3 pins [form=molex]
  LED1 = smd LED [color="Green (565nm)" package="1206 [SMD]"]
  LED2 = smd LED [color="Green (565nm)" package="1206 [SMD]"]
  LED5 = smd LED [color="Yellow (585nm)" package="1206 [SMD]"]
  LED3 = smd LED [color="Green (565nm)" package="1206 [SMD]"]
  LED4 = smd LED [color="Green (565nm)" package="1206 [SMD]"]
  J1 = molex pin header, 5 pins [form=molex]
  U4 = Voltage Regulator - 5V [part_number=L7805CDT-TR package="DPak [SMD]"]
  C7 = Ceramic Capacitor [capacitance=1µF package="1206 [SMD, multilayer]"]
  J-D = molex pin header, 5 pins [form=molex]
  C1 = Ceramic Capacitor [capacitance=1µF package="1206 [SMD, multilayer]"]
  C3 = Ceramic Capacitor [capacitance=1µF package="1206 [SMD, multilayer]"]
  C5 = Ceramic Capacitor [capacitance=1µF package="1206 [SMD, multilayer]"]
  U3 = Voltage Regulator - 5V [part_number=L7805CDT-TR package="DPak [SMD]"]
  U2 = Voltage Regulator - 5V [part_number=L7805CDT-TR package="DPak [SMD]"]
  U1 = Voltage Regulator - 5V [part_number=L7805CDT-TR package="DPak [SMD]"]
  J-C = molex pin header, 5 pins [form=molex]
  J-B = molex pin header, 5 pins [form=molex]
  J-A = molex pin header, 5 pins [form=molex]
  J3/TP = molex pin header, 3 pins [form=molex]

nets:
  GND: C2.0, C4.0, C6.0, C8.0, C9.0, J2/PWR.pin1, J2/PWR.pin3, LED1.cathode, LED2.cathode, LED5.cathode, LED3.cathode, LED4.cathode, J1.pin1, U4.GND, C7.0, J-D.pin1, C1.0, C3.0, C5.0, U3.GND, U2.GND, U1.GND, J-C.pin1, J-B.pin1, J-A.pin1, J3/TP.pin1
  VCC_A: C2.1, R1.Pin_1, C9.1, J1.pin2, U1.output_voltage, J-A.pin2
  N1: R1.Pin_0, LED1.anode
  N2: C4.1, R2.Pin_1, U2.output_voltage, J-B.pin2
  N3: R2.Pin_0, LED2.anode
  N4: C6.1, R3.Pin_1, U3.output_voltage, J-C.pin2
  N5: R3.Pin_0, LED3.anode
  VCC_D: C8.1, R4.Pin_1, U4.output_voltage, J-D.pin2, J3/TP.pin2
  N6: R4.Pin_0, LED4.anode
  N7: R5.Pin_0, LED5.anode
  CLUSTER_SYNC: R5.Pin_1, J1.pin3, J-D.pin3, J-C.pin3, J-B.pin3, J-A.pin3
  7.5V: J2/PWR.pin2, U4.input_voltage, C7.1, C1.1, C3.1, C5.1, U3.input_voltage, U2.input_voltage, U1.input_voltage, J3/TP.pin3
  CLUSTER_SDA: J1.pin4, J-D.pin4, J-C.pin4, J-B.pin4, J-A.pin4
  CLUSTER_SCL: J1.pin5, J-D.pin5, J-C.pin5, J-B.pin5, J-A.pin5

notes:
  CodeValue ClockWall
  Power & Signal Distribution
  v1.2, 2018-02-08
  +7v5
  GND
  +5
  +12v
  Jack-A ... to Clock Module Boards 0, 1, 2, 3
  Jack-B ... to Clock Module Boards 4, 5, 6, 7
  Jack-C ... to Clock Module Boards 8, 9, 10, 11
  Jack-D ... to Clock Module Boards 12, 13, 14, 15
  ClockWall, CLockWall Power & Signal Distribution PCB, 1.2
  Jack-1 ... to Cluster Controller Board
  test point
  SYNC
  SDA
  SCL
  SYNC->
  PWR-A
  PWR-B
  PWR-C
  PWR-D
  •
