# Fritzing sketch cluster_controller_v1.1 (saved by Fritzing 0.9.3b)
circuit board: 5cm x 10cm
breadboards: 1

parts:
  SW1 = DIP Switch 4 Position [part_number="C&K BD04 or equiv." package=dipswitch-04]
  C1 = Electrolytic Capacitor [capacitance=47µF voltage=16V package="0605 [SMD, electrolytic]"]
  J1 = molex pin header, 5 pins [form=molex part_number=B5B-XH-A]
  Arduino = Arduino Nano (Rev3.0) (ICSP) [part_number=Nano]
  C2 = Ceramic Capacitor [capacitance=1µF package="1206 [SMD, multilayer]"]
  R1 = Resistor [tolerance=±1% resistance=4.7k package="1206 [SMD]"]
  R2 = Resistor [tolerance=±1% resistance=4.7k package="1206 [SMD]"]

nets:
  GND: SW1.1, SW1.2, SW1.3, SW1.4, C1.-, J1.pin1, Arduino.GND, C2.0
  SW_B1: SW1.5, Arduino.A2
  SW_B2: SW1.6, Arduino.A3
  SW_B4: SW1.7, Arduino.A6
  SW_B8: SW1.8, Arduino.A7
  5V/REG. +5v: C1.+, J1.pin2, Arduino.5V, C2.1, R1.Pin_1, R2.Pin_1
  CLSTR_SYNC: J1.pin3, Arduino.D2
  CLSTR_SDA: J1.pin4, Arduino.A4, R2.Pin_0
  CLSTR_SCL: J1.pin5, Arduino.A5, R1.Pin_0
  SS_: Arduino.D10
  MISO/MOSI: Arduino.D11/MOSI, Arduino.D12/MISO
  SCLK: Arduino.D13/SCK

notes:
  SIG-in / (signal in)
  1 - GND
  2 - +5
  3 - Sync/D2
  4 - SDA/D4
  5 - SCL/D5
  A2
  PCBA, Cluster Controller
  Gnd
  Reg. +5V
  CLSTR_SYNC
  CLSTR_SDA
  CLSTR_CLK
  ID SWITCH
  8  4  2  1
  ID SWITCH
  1 - ID-bit 3 MSB
  2 - ID-bit 2
  3 - ID-bit 1
  4 - ID-bit 0 LSB
  MOSI
  OE
  LATCH
  SCLK
  REV: 1.1
  SN: 1.5
  © CodeValue, Ltd., 2018
  Clockwall Cluster Controller Board
