# Fritzing sketch clockwall element (saved by Fritzing 0.9.2b)
breadboards: 1

parts:
  Part1 = Motor Driver 1A Dual TB6612FNG
  U1 = 74HC595 [package="DIP16 [THT]"]
  IC1 = IC, DIP package, 14 pins [chip_label=74HC243]
  JP1 = Header 4 [package=molex-1x4_lock]  # not connected

nets:
  GND: Part1.GND, U1.GND
  VCC: Part1.VCC, Part1.VM, U1.MR, U1.VCC
  N1: U1.OE, IC1.pin4
  N2: U1.DS, IC1.pin3
