# Fritzing sketch 4_clock_module (saved by Fritzing 0.9.3b)
circuit board: 40.5cm x 4.8cm
breadboards: 2

parts:
  DATA_IN = Header 4 [package=screwterminal-3.5mm-4_lock]
  DATA_OUT = Header 4 [package=screwterminal-3.5mm-4_lock]
  IC5 = SHIFT REGISTER [package=dil16]
  IC4 = SHIFT REGISTER [package=dil16]
  M1 = Stepper Motor - Automotive Gauge
  M2 = Stepper Motor - Automotive Gauge
  M3 = Stepper Motor - Automotive Gauge
  M4 = Stepper Motor - Automotive Gauge
  M5 = Stepper Motor - Automotive Gauge
  M6 = Stepper Motor - Automotive Gauge
  M7 = Stepper Motor - Automotive Gauge
  M8 = Stepper Motor - Automotive Gauge
  IC1 = SHIFT REGISTER [package=dil16]
  IC2 = SHIFT REGISTER [package=dil16]
  IC3 = SHIFT REGISTER [package=dil16]
  IC6 = SHIFT REGISTER [package=dil16]
  IC7 = SHIFT REGISTER [package=dil16]
  IC8 = SHIFT REGISTER [package=dil16]
  IC9 = DIP - 20 pins [chip_label=74HC245 package="DIP (Dual Inline) [THT]"]
  PWR_OUT = Header 2 [package=jst-2-pth-ns]
  PWR_IN = Header 2 [package=jst-2-pth-ns]

nets:
  N1: DATA_IN.1, IC9.A0
  N2: DATA_IN.2, IC9.A2
  N3: DATA_IN.3, IC9.A4
  N4: DATA_IN.4, IC9.A6
  N5: DATA_OUT.1, IC8.QH*
  N6: DATA_OUT.2, IC5.G, IC4.G, IC1.G, IC2.G, IC3.G, IC6.G, IC7.G, IC8.G, IC9.B2
  N7: DATA_OUT.3, IC5.RCK, IC4.RCK, IC1.RCK, IC2.RCK, IC3.RCK, IC6.RCK, IC7.RCK, IC8.RCK, IC9.B4
  N8: DATA_OUT.4, IC5.SCK, IC4.SCK, IC1.SCK, IC2.SCK, IC3.SCK, IC6.SCK, IC7.SCK, IC8.SCK, IC9.B6
  N9: IC5.QE, M5.pin_3
  N10: IC5.QF, M5.pin_4
  N11: IC5.QG, M5.pin_2
  N12: IC5.QH, M5.pin_1
  GND: IC5.GND, IC4.GND, IC1.GND, IC2.GND, IC3.GND, IC6.GND, IC7.GND, IC8.GND, IC9.GND, IC9.OE, PWR_OUT.1, PWR_IN.1
  N13: IC5.QH*, IC6.SER
  5V: IC5.SCL, IC5.VCC, IC4.SCL, IC4.VCC, IC1.SCL, IC1.VCC, IC2.SCL, IC2.VCC, IC3.SCL, IC3.VCC, IC6.SCL, IC6.VCC, IC7.SCL, IC7.VCC, IC8.SCL, IC8.VCC, IC9.DIR, IC9.Vcc, PWR_OUT.2, PWR_IN.2
  N14: IC5.SER, IC4.QH*
  N15: IC4.QE, M4.pin_2
  N16: IC4.QF, M4.pin_1
  N17: IC4.QG, M4.pin_3
  N18: IC4.QH, M4.pin_4
  N19: IC4.SER, IC3.QH*
  N20: M1.pin_1, IC1.QH
  N21: M1.pin_2, IC1.QG
  N22: M1.pin_3, IC1.QE
  N23: M1.pin_4, IC1.QF
  N24: M2.pin_1, IC2.QF
  N25: M2.pin_2, IC2.QE
  N26: M2.pin_3, IC2.QG
  N27: M2.pin_4, IC2.QH
  N28: M3.pin_1, IC3.QH
  N29: M3.pin_2, IC3.QG
  N30: M3.pin_3, IC3.QE
  N31: M3.pin_4, IC3.QF
  N32: M6.pin_1, IC6.QF
  N33: M6.pin_2, IC6.QE
  N34: M6.pin_3, IC6.QG
  N35: M6.pin_4, IC6.QH
  N36: M7.pin_1, IC7.QH
  N37: M7.pin_2, IC7.QG
  N38: M7.pin_3, IC7.QE
  N39: M7.pin_4, IC7.QF
  N40: M8.pin_1, IC8.QF
  N41: M8.pin_2, IC8.QE
  N42: M8.pin_3, IC8.QG
  N43: M8.pin_4, IC8.QH
  N44: IC1.QH*, IC2.SER
  N45: IC1.SER, IC9.B0
  N46: IC2.QH*, IC3.SER
  N47: IC6.QH*, IC7.SER
  N48: IC7.QH*, IC8.SER

notes:
  1 DATA_IN
  2 OE*
  3 STORE
  4 SCLK
  1 DATA_OUT
  2 OE*
  3 STORE
  4 SCLK
  JST XH2.54 2pin, through-hole shrouded header
  board: 4-pin header;
  cable: JST RE2.54 4pin connector
  pin1 GND
  pin2 Vcc
  Vcc
  GND
  DO OE ST CP
  DI OE ST CP

custom parts:
  Stepper Motor - Automotive Gauge: Simple, Automotive Gauge stepper motor
  DIP - 20 pins: A DIP stand-in part for whatever IC you want. With 20 pins on a 300mil dual inline package (DIP) footprint.
