# Fritzing sketch test (saved by Fritzing 0.9.3b)
breadboards: 1

parts:
  Part1 = Arduino Nano (Rev3.0)
  SW1 = DIP Switch 8 Position [package=dipswitch-08]  # not connected
  U1 = Motor- VID28 [part_number=VID28-05 package=motor-64mm]

nets:
  N1: Part1.A2, U1.pin_A4
  N2: Part1.A1, U1.pin_A3
  N3: Part1.A0, U1.pin_B2
  N4: Part1.AREF, U1.pin_B1

custom parts:
  Motor- VID28: VID28-05 motor
