# Fritzing sketch clock module cable, 2.54mm (saved by Fritzing 0.9.3b)

parts:
  J1 = female pin header, 5 pins [form="♀ (female)"]
  J2 = female pin header, 5 pins [form="♀ (female)"]

nets:
  N1: J1.pin1, J2.pin5
  N2: J1.pin2, J2.pin4
  N3: J1.pin3, J2.pin3
  N4: J1.pin4, J2.pin2
  N5: J1.pin5, J2.pin1

notes:
  CABLE DRAWING, Clock Module Cable
